# Fritzing sketch FeatherM0_Davis_ISS_Ethernet (saved by Fritzing 1.0.0rc)
breadboards: 4

parts:
  Part1 = Adafruit Feather M0 RFM69 [part_number="Adafruit #3176 or #3177"]
  Part2 = Adafruit Ethernet FeatherWing [part_number="Adafruit #3201"]
  Part3 = Adafruit Adalogger FeatherWing [part_number="Adafruit #2922"]
  Part4 = Adafruit OLED FeatherWing [part_number="Adafruit #2900"]

nets:
  N1: Part1.MISO, Part2.MISO, Part3.MISO
  N2: Part1.MOSI, Part2.MOSI, Part3.MOSI
  N3: Part1.SCK, Part2.SCK, Part3.SCK
  GND: Part1.GND, Part2.GND, Part3.GND, Part4.GND
  N4: Part1.D10, Part2.K
  N5: Part1.D9, Part3.L
  N6: Part1.SCL, Part3.SCL, Part4.SCL
  N7: Part1.SDA, Part3.SDA, Part4.SDA
  3.3V: Part2.3.3V, Part3.+3V3, Part4.3.3V

custom parts:
  Adafruit Feather M0 RFM69: This is the Adafruit Feather M0 RFM69 Packet Radio - our take on an microcontroller with a RFM69HCW packet radio transceiver plus built in USB and battery charging. Its an Adafruit Feather M0 with a 433MHz or 900MHz radio module cooked in! We have other boards in the Feather family, check'em out here. At the Feather M0's heart is an ATSAMD21G18 ARM Cortex M0 processor, clocked at 48 MHz and at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
  Adafruit Ethernet FeatherWing: Wireless is wonderful, but sometimes you want the strong reliability of a wire. If your Feather board is going to be part of a permanent installation, this Ethernet FeatherWing will let you add quick and easy wired Internet. Just plug in a standard ethernet cable, and run the Ethernet2 library for cross-platform networking. Ethernet is a tried-and-true networking standard. It's supported by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
  Adafruit Adalogger FeatherWing: This is the Adalogger FeatherWing: it adds both a battery-backed Real Time Clock and micro SD card storage to any Feather main board. This FeatherWing will make it real easy to add datalogging to any of our existing Feathers. You get both an I2C real time clock (PCF8523) with 32KHz crystal and battery backup, and a microSD socket that connects to the SPI port pins (+ extra pin for CS). Tested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
  Adafruit OLED FeatherWing: This is the FeatherWing OLED: it adds a 128x32 monochrome OLED plus 3 user buttons to any Feather main board. These displays are small, only about 1" diagonal, but very readable due to the high contrast of an OLED display. This screen is made of 128x32 individual white OLED pixels and because the display makes its own light, no backlight is required. This reduces the power required to run the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
